# Fritzing sketch schematic (saved by Fritzing 0.9.3b)

parts:
  Part1 = Arduino Nano (Rev3.0)  # not connected
  Part2 = Arduino Nano (Rev3.0)
  Part3 = NRF24L01+ Breakout Board

nets:
  N1: Part2.D9, Part3.CE
  N2: Part2.D10, Part3.CS
  N3: Part2.D11/MOSI, Part3.MOSI
  N4: Part2.D12/MISO, Part3.MISO
  GND: Part2.GND, Part3.GND
  3V3: Part2.3V3, Part3.VCC
  N5: Part2.D13/SCK, Part3.SCK
